// Logisim project NanoSwitch16.circ as structural Verilog: 2 circuits, main circuit main
module main (
  input  [3:0] in_1,
  output _0000,
  output _0001,
  output _0010,
  output _0011,
  output _0100,
  output _0101,
  output _0110,
  output [3:0] out_9,
  output _0111,
  output _1000,
  output _1001,
  output _1010,
  output _1011,
  output _1100,
  output _1101,
  output _1110,
  output _1111
);

  wire adder_1_y, adder_2_x, adder_2_y, adder_3_x, adder_3_y, adder_4_x, adder_4_y, and_1_out, clock_1_out,
       d_ff_1_q, d_ff_1_qn, d_ff_6_q, d_ff_7_q, d_ff_8_q, d_ff_9_q, d_ff_10_q, d_ff_11_q, d_ff_12_q,
       d_ff_13_q, execute_puls_out, not_1_out, not_2_out, not_3_out, not_4_out, not_5_out, not_6_out;
  wire [3:0] d_ff_14_q;
  wire [7:0] ram_1_dout;

  Clock clock_1 (.out(clock_1_out));
  and execute_puls (execute_puls_out, clock_1_out, d_ff_1_qn);
  not not_1 (not_1_out, d_ff_1_q);
  D_Flip_Flop d_ff_1 (.D(not_1_out), .clk(clock_1_out), .Q(d_ff_1_q), .Qn(d_ff_1_qn));  // open: preset, reset
  D_Flip_Flop d_ff_2 (.D(d_ff_6_q), .clk(d_ff_1_qn), .Q(out_9[3]));  // open: Qn, preset, reset
  D_Flip_Flop d_ff_3 (.D(d_ff_7_q), .clk(d_ff_1_qn), .Q(out_9[2]));  // open: Qn, preset, reset
  D_Flip_Flop d_ff_4 (.D(d_ff_8_q), .clk(d_ff_1_qn), .Q(out_9[1]));  // open: Qn, preset, reset
  D_Flip_Flop d_ff_5 (.D(d_ff_9_q), .clk(d_ff_1_qn), .Q(out_9[0]));  // open: Qn, preset, reset
  RAM ram_1 (.addr({in_1, out_9}), .oe(1'b1), .clk(clock_1_out), .dout(ram_1_dout));  // open: we, din
  adder adder_1 (.a(out_9[3]), .b(adder_2_x), .y(adder_1_y));  // open: x
  adder adder_2 (.a(out_9[2]), .b(adder_3_x), .x(adder_2_x), .y(adder_2_y));
  adder adder_3 (.a(out_9[1]), .b(adder_4_x), .x(adder_3_x), .y(adder_3_y));
  adder adder_4 (.a(out_9[0]), .b(1'b1), .x(adder_4_x), .y(adder_4_y));
  not not_2 (not_2_out, clock_1_out);
  D_Flip_Flop d_ff_6 (.D(adder_1_y), .clk(clock_1_out), .Q(d_ff_6_q));  // open: Qn, preset, reset
  D_Flip_Flop d_ff_7 (.D(adder_2_y), .clk(clock_1_out), .Q(d_ff_7_q));  // open: Qn, preset, reset
  D_Flip_Flop d_ff_8 (.D(adder_3_y), .clk(clock_1_out), .Q(d_ff_8_q));  // open: Qn, preset, reset
  D_Flip_Flop d_ff_9 (.D(adder_4_y), .clk(clock_1_out), .Q(d_ff_9_q));  // open: Qn, preset, reset
  and and_1 (and_1_out, d_ff_1_q, not_2_out);
  D_Flip_Flop d_ff_10 (.D(ram_1_dout[4]), .clk(and_1_out), .Q(d_ff_10_q));  // open: Qn, preset, reset
  D_Flip_Flop d_ff_11 (.D(ram_1_dout[5]), .clk(and_1_out), .Q(d_ff_11_q));  // open: Qn, preset, reset
  D_Flip_Flop d_ff_12 (.D(ram_1_dout[6]), .clk(and_1_out), .Q(d_ff_12_q));  // open: Qn, preset, reset
  D_Flip_Flop d_ff_13 (.D(ram_1_dout[7]), .clk(and_1_out), .Q(d_ff_13_q));  // open: Qn, preset, reset
  D_Flip_Flop d_ff_14 (.D(ram_1_dout[0]), .clk(and_1_out), .Q(d_ff_14_q[0]));  // open: Qn, preset, reset
  D_Flip_Flop d_ff_15 (.D(ram_1_dout[1]), .clk(and_1_out), .Q(d_ff_14_q[1]));  // open: Qn, preset, reset
  D_Flip_Flop d_ff_16 (.D(ram_1_dout[2]), .clk(and_1_out), .Q(d_ff_14_q[2]));  // open: Qn, preset, reset
  D_Flip_Flop d_ff_17 (.D(ram_1_dout[3]), .clk(and_1_out), .Q(d_ff_14_q[3]));  // open: Qn, preset, reset
  not not_3 (not_3_out, d_ff_13_q);
  not not_4 (not_4_out, d_ff_12_q);
  not not_5 (not_5_out, d_ff_11_q);
  not not_6 (not_6_out, d_ff_10_q);
  and and_2 (_0000, not_6_out, not_5_out, execute_puls_out, not_4_out, not_3_out);
  and and_3 (_0001, d_ff_10_q, not_5_out, execute_puls_out, not_4_out, not_3_out);
  and and_4 (_0010, not_6_out, d_ff_11_q, execute_puls_out, not_4_out, not_3_out);
  and and_5 (_0011, d_ff_10_q, d_ff_11_q, execute_puls_out, not_4_out, not_3_out);
  and and_6 (_0100, not_6_out, not_5_out, execute_puls_out, d_ff_12_q, not_3_out);
  and and_7 (_0101, d_ff_10_q, not_5_out, execute_puls_out, d_ff_12_q, not_3_out);
  and and_8 (_0110, not_6_out, d_ff_11_q, execute_puls_out, d_ff_12_q, not_3_out);
  and and_9 (_0111, d_ff_10_q, d_ff_11_q, execute_puls_out, d_ff_12_q, not_3_out);
  and and_10 (_1000, not_6_out, not_5_out, execute_puls_out, not_4_out, d_ff_13_q);
  and and_11 (_1001, d_ff_10_q, not_5_out, execute_puls_out, not_4_out, d_ff_13_q);
  and and_12 (_1010, not_6_out, d_ff_11_q, execute_puls_out, not_4_out, d_ff_13_q);
  and and_13 (_1011, d_ff_10_q, d_ff_11_q, execute_puls_out, not_4_out, d_ff_13_q);
  and and_14 (_1100, not_6_out, not_5_out, execute_puls_out, d_ff_12_q, d_ff_13_q);
  and and_15 (_1101, d_ff_10_q, not_5_out, execute_puls_out, d_ff_12_q, d_ff_13_q);
  and and_16 (_1110, not_6_out, d_ff_11_q, execute_puls_out, d_ff_12_q, d_ff_13_q);
  and and_17 (_1111, d_ff_10_q, d_ff_11_q, execute_puls_out, d_ff_12_q, d_ff_13_q);
  LedBar #(.matrixcols(4)) ledbar_1 (
    .led0(d_ff_14_q[0]), .led1(d_ff_14_q[1]), .led2(d_ff_14_q[2]), .led3(d_ff_14_q[3]));

  // Notes on the sheet:
  //   fetch register
  //   page
  //   opcode
  //   operand
  //   Instruction register
  //   Operand
  //   instruction decoder
endmodule

module adder (
  input  a,
  input  b,
  output x,
  output y
);

  wire and_2_out, and_3_out, not_1_out, not_2_out;

  not not_1 (not_1_out, a);
  not not_2 (not_2_out, b);
  and and_1 (x, a, b);
  and and_2 (and_2_out, a, not_2_out);
  and and_3 (and_3_out, not_1_out, b);
  or or_1 (y, and_2_out, and_3_out);
endmodule
